# Fritzing sketch skysweeper_done (saved by Fritzing 0.9.3b)
breadboards: 1

parts:
  Raspberry_Pi_1 = Raspberry Pi 3 [part_number=RPI-3-V1.2]
  LED2 = LED - 5mm [color="Red (633nm)" package="5 mm [THT]"]
  R2 = Resistor [tolerance=±5% resistance=220 package=THT]
  LED3 = LED - 5mm [color="Red (633nm)" package="5 mm [THT]"]
  R3 = Resistor [tolerance=±5% resistance=220 package=THT]
  LED4 = LED - 5mm [color="Red (633nm)" package="5 mm [THT]"]
  R4 = Resistor [tolerance=±5% resistance=220 package=THT]
  R5 = Resistor [tolerance=±5% resistance=220 package=THT]
  LED25 = LED - 5mm [color="Red (633nm)" package="5 mm [THT]"]
  R6 = Resistor [tolerance=±5% resistance=220 package=THT]
  R7 = Resistor [tolerance=±5% resistance=220 package=THT]
  R8 = Resistor [tolerance=±5% resistance=220 package=THT]
  R9 = Resistor [tolerance=±5% resistance=220 package=THT]
  R10 = Resistor [tolerance=±5% resistance=220 package=THT]
  R11 = Resistor [tolerance=±5% resistance=220 package=THT]
  R12 = Resistor [tolerance=±5% resistance=220 package=THT]
  LED17 = LED - 5mm [color="Yellow (595nm)" package="5 mm [THT]"]
  LED19 = LED - 5mm [color="Yellow (595nm)" package="5 mm [THT]"]
  LED20 = LED - 5mm [color="Yellow (595nm)" package="5 mm [THT]"]
  LED22 = LED - 5mm [color="Green (555nm)" package="5 mm [THT]"]
  LED23 = LED - 5mm [color="Green (555nm)" package="5 mm [THT]"]
  LED24 = LED - 5mm [color="White (4500K)" package="5 mm [THT]"]
  LED18 = LED - 5mm [color="Yellow (595nm)" package="5 mm [THT]"]

nets:
  N1: Raspberry_Pi_1.GND, R2.Pin_1, R3.Pin_1, R4.Pin_1, R5.Pin_1, R6.Pin_1, R7.Pin_0, R8.Pin_0, R9.Pin_0, R10.Pin_0, R11.Pin_0, R12.Pin_0
  N2: Raspberry_Pi_1.GPIO5, LED25.anode
  N3: Raspberry_Pi_1.GPIO6, LED4.anode
  N4: Raspberry_Pi_1.GPIO13, LED3.anode
  N5: Raspberry_Pi_1.GPIO19, LED2.anode
  N6: Raspberry_Pi_1.GPIO26, LED24.anode
  N7: Raspberry_Pi_1.GPIO25, LED23.anode
  N8: Raspberry_Pi_1.GPIO24, LED22.anode
  N9: Raspberry_Pi_1.GPIO23, LED20.anode
  N10: Raspberry_Pi_1.GPIO18, LED19.anode
  N11: Raspberry_Pi_1.GPIO15, LED18.anode
  N12: Raspberry_Pi_1.GPIO14, LED17.anode
  N13: LED2.cathode, R2.Pin_0
  N14: LED3.cathode, R3.Pin_0
  N15: LED4.cathode, R4.Pin_0
  N16: R5.Pin_0, LED25.cathode
  N17: R6.Pin_0, LED24.cathode
  N18: R7.Pin_1, LED17.cathode
  N19: R8.Pin_1, LED18.cathode
  N20: R9.Pin_1, LED19.cathode
  N21: R10.Pin_1, LED20.cathode
  N22: R11.Pin_1, LED22.cathode
  N23: R12.Pin_1, LED23.cathode
